# Fritzing sketch Untitled Sketch 2 (saved by Fritzing 0.9.3b)
circuit board: 8.46667cm x 5.64444cm

parts:
  U2 = ESP32-38PinWide [part_number=ESP32-38PinWide]
  IC1 = Nextion SPI 2.4" LCD NX3224T024_011

nets:
  N1: U2.3.3, IC1.VCC
  N2: U2.EN, IC1.pin2
  N3: U2.GPIO36, IC1.pin3
  GND: U2.GND, IC1.GND

custom parts:
  ESP32-38PinWide: Generic 38-Pin ESP32 with wide format (only access to one side of pins on a breadboard) based on Stephen Lilley's HiLetgo ESP-WROOM-32 ESP32 ESP-32S Development Board.
